# Fritzing sketch robot (saved by Fritzing 0.8.7b)
breadboards: 1

parts:
  SparkFun_micro_bit_Breakout1 = SparkFun micro:bit Breakout [part_number=BOB-13988]
  Mod1 = Microbit
  M2 = DC Motor
  U1 = HC-SR04 [chip_label=IC package="SIP (Single Inline) [THT]"]
  R2 = Resistor [tolerance=±5% resistance=1k package=THT]
  R3 = Resistor [tolerance=±5% resistance=2.2k package=THT]
  IC1 = L293D [package=THT]
  VCC1 = 4 x AAA Battery Mount
  J1 = Basic Servo
  J2 = Basic Servo
  M1 = DC Motor
  VCC2 = Battery

nets:
  GND: SparkFun_micro_bit_Breakout1.GND, U1.GND, R3.Pin_1, IC1.0V, VCC1.-, J1.gnd, J2.gnd
  N1: SparkFun_micro_bit_Breakout1.B6, Mod1.P20, Mod1.GND, Mod1.Bat_-, VCC2.-
  N2: SparkFun_micro_bit_Breakout1.B8, SparkFun_micro_bit_Breakout1.B14, Mod1.P16, Mod1.3V3, Mod1.P19
  N3: SparkFun_micro_bit_Breakout1.B16, Mod1.P14, Mod1.P15
  N4: SparkFun_micro_bit_Breakout1.B18, Mod1.P13
  N5: SparkFun_micro_bit_Breakout1.B20, Mod1.P2
  N6: SparkFun_micro_bit_Breakout1.B22, Mod1.P12
  N7: SparkFun_micro_bit_Breakout1.B24, Mod1.P10, Mod1.P11
  N8: SparkFun_micro_bit_Breakout1.B26, Mod1.P8, Mod1.P9
  N9: SparkFun_micro_bit_Breakout1.B32, Mod1.P6, Mod1.P7
  N10: SparkFun_micro_bit_Breakout1.B34, Mod1.P4, Mod1.P5
  N11: SparkFun_micro_bit_Breakout1.B40, Mod1.P3
  N12: SparkFun_micro_bit_Breakout1.0, IC1.Enable_1, IC1.Enable_2
  N13: SparkFun_micro_bit_Breakout1.1, J1.pulse
  N14: SparkFun_micro_bit_Breakout1.2, J2.pulse
  N15: SparkFun_micro_bit_Breakout1.8, U1.Trig
  N16: SparkFun_micro_bit_Breakout1.12, R2.Pin_0, R3.Pin_0
  N17: SparkFun_micro_bit_Breakout1.13, IC1.In_2
  N18: SparkFun_micro_bit_Breakout1.14, IC1.In_1
  N19: SparkFun_micro_bit_Breakout1.15, IC1.In_3
  N20: SparkFun_micro_bit_Breakout1.16, IC1.In_4
  N21: Mod1.Bat_+, VCC2.+
  N22: M2.pin_1, IC1.Out_3_(_Controlled_by_Enable_2_)
  N23: M2.pin_2, IC1.Out_4_(_Controlled_by_Enable_2_)
  VCC: U1.Vcc, IC1.+Vmotor, IC1.+V, VCC1.+, J1.vcc, J2.vcc
  N24: U1.Echo, R2.Pin_1
  N25: IC1.Out_1_(_Controlled_by_Enable_1_), M1.pin_2
  N26: IC1.Out_2_(_Controlled_by_Enable_1_), M1.pin_1

custom parts:
  SparkFun micro:bit Breakout: The micro:bit breakout is a board that connects to the BBC micro:bit and expands the capabilities of the development platform by providing access to more pins and allowing for connections to the I2C and SPI buses. This breakout board for the micro:bit’s edge connector allows intermediate and advanced users to connect the micro:bit to breadboards and other sensors, motors, LEDs, and more! The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
  Microbit: BBC Microbit Fritzing part. May 2019 expanded to include schematic and pcb views as well as breadboard. PCB view assumes an Adafruit PRODUCT ID: 3342 2x40 Right Angle through hole edge connector (although others will probably work as well). The pcb svg is custom (see forum article http://forum.fritzing.org/t/making-edge-connectors-and-both-side-smd-parts/7287 for an explaination if you need to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
  HC-SR04: HC-SR04 ultrasound distance sensor
